# Fritzing sketch CarbOnBal (saved by Fritzing 0.9.3b)
circuit board: 8.46667cm x 5.64444cm
breadboards: 1

parts:
  U1 = AD22100 - Voltage Output Temperature Sensor with Signal Conditioning [part_number=MAP]
  S3_UP_/_Contrast = SWITCH-MOMENTARY-2 [package=tactile-pth]
  C1 = Electrolytic Capacitor [capacitance=47µF voltage=10V package="1010 [SMD, electrolytic]"]
  R3 = Resistor [tolerance=±5% resistance=1k package=THT]
  S1_CANCEL_/_Freeze = SWITCH-MOMENTARY-2 [package=tactile-pth]
  U2 = AD22100 - Voltage Output Temperature Sensor with Signal Conditioning [part_number=MAP]
  LCD1 = LCD screen
  U4 = AD22100 - Voltage Output Temperature Sensor with Signal Conditioning [part_number=MAP]
  Part1 = Arduino Nano (Rev3.0)
  U3 = AD22100 - Voltage Output Temperature Sensor with Signal Conditioning [part_number=MAP]
  U5 = 74HC595 [package="DIP16 [THT]"]
  S2_DOWN_/_Brightness_(REVS) = SWITCH-MOMENTARY-2 [package=tactile-pth]
  S4_OK_/_Menu = SWITCH-MOMENTARY-2 [package=tactile-pth]
  R4 = Resistor [tolerance=±20% resistance=330 package=THT]
  C2 = Ceramic Capacitor [capacitance=100nF package="100 mil [THT, multilayer]"]

nets:
  VDD: U1.V+, U2.V+, LCD1.VDD, LCD1.DB0, LCD1.DB1, LCD1.DB2, LCD1.DB3, U4.V+, Part1.5V, U3.V+, U5.MR, U5.VCC, C2.0
  N1: U1.Vo, Part1.A0
  GND: U1.GND, S3_UP_/_Contrast.2, C1.-, S1_CANCEL_/_Freeze.2, U2.GND, LCD1.VSS, LCD1.R/W, LCD1.LED-, U4.GND, Part1.GND, U3.GND, U5.GND, U5.OE, S2_DOWN_/_Brightness_(REVS).2, S4_OK_/_Menu.2, C2.1
  N2: S3_UP_/_Contrast.1, Part1.D2
  N3: C1.+, R3.Pin_1, LCD1.V0
  N4: R3.Pin_0, Part1.D5
  N5: S1_CANCEL_/_Freeze.1, Part1.D0/RX
  N6: U2.Vo, Part1.A1
  N7: LCD1.RS, U5.Q1
  N8: LCD1.E, Part1.D8, U5.Q3
  N9: LCD1.DB4, U5.Q4
  N10: LCD1.DB5, U5.Q5
  N11: LCD1.DB6, U5.Q6
  N12: LCD1.DB7, U5.Q7
  N13: LCD1.LED+, R4.Pin_1
  N14: U4.Vo, Part1.A3
  N15: Part1.D1/TX, S2_DOWN_/_Brightness_(REVS).1
  N16: Part1.D3, S4_OK_/_Menu.1
  N17: Part1.D6, R4.Pin_0
  N18: Part1.D9, U5.ST_CP
  N19: Part1.D11/MOSI, U5.DS
  N20: Part1.A2, U3.Vo
  N21: Part1.D13/SCK, U5.SH_CP

notes:
  Open Hardware: Cern-OHL
  CarbOnBal
  v 1.0
  Copyright 2017
  L.L.M. (Dennis) Meulensteen
